// Logisim project voice_circuit_v24_perfect.circ as structural Verilog: 1 circuit, main circuit main
module main (
  input  A,
  input  B,
  input  C,
  output Y
);

  wire AB, notC;

  and and_1 (AB, A, B);
  not not_1 (notC, C);
  or or_1 (Y, AB, notC);
endmodule
